// Logisim project CPU.circ as structural Verilog: 2 circuits, main circuit main
module main (
  output [7:0] address,
  output [1:0] addrsel,
  output [7:0] r0,
  output [7:0] r1,
  output [7:0] r2,
  output [7:0] r3,
  output [7:0] datain,
  output [7:0] Result,
  output [7:0] dval,
  output [1:0] destregsel,
  output [7:0] sbus,
  output [7:0] dbus,
  output [1:0] aluop,
  output pcsel,
  output [1:0] phase,
  output pcload,
  output Carry_out,
  output Zero,
  output Overflow,
  output Negative
);

  wire clock_1_out, clock_2_out, clock_3_out, clock_4_out, dwrite, immload, irload, read_write,
       registerfiles_1_negative, registerfiles_1_zero;
  wire [1:0] regsel, sourceregsel;
  wire [7:0] multiplexer_3_out, pc_adder_1_pc_out, register_1_q, register_2_q, register_3_q;

  RAM #(.bus("separate")) ram_1 (
    .addr(address), .din(dbus), .data(datain), .str(read_write), .clk(clock_1_out));  // open: sel, ld, clr
  Clock clock_1 (.out(clock_1_out));
  Clock clock_2 (.out(clock_2_out));
  Register register_1 (.D(datain), .en(irload), .Q(register_1_q), .clk(clock_3_out));  // open: clr
  Clock clock_3 (.out(clock_3_out));
  Decode_Logic decode_logic_1 (
    .addrsel(addrsel), .irvalue(register_1_q), .irload(irload), .immload(immload), .dwrite(dwrite),
    .destregsel(destregsel), .sourceregsel(sourceregsel), .aluop(aluop), .regsel(regsel), .phase(phase),
    .read_write(read_write), .pcsel(pcsel), .zero(registerfiles_1_zero), .negative(registerfiles_1_negative),
    .pcload(pcload));
  Multiplexer #(.select(2), .width(8), .enable("false")) multiplexer_1 (
    .in0(register_3_q), .in1(register_2_q), .in2(sbus), .in3(dbus), .out(address), .sel(addrsel));
  Register register_2 (.D(datain), .en(immload), .Q(register_2_q), .clk(clock_2_out));  // open: clr
  PC_Adder pc_adder_1 (.PC_in(register_3_q), .PC_out(pc_adder_1_pc_out));
  Multiplexer #(.select(2), .width(8), .enable("false")) multiplexer_2 (
    .in0(register_2_q), .in1(sbus), .in2(datain), .in3(Result), .out(dval), .sel(regsel));
  Multiplexer #(.width(8), .enable("false")) multiplexer_3 (
    .in0(register_2_q), .in1(pc_adder_1_pc_out), .out(multiplexer_3_out), .sel(pcsel));
  Register register_3 (.D(multiplexer_3_out), .en(pcload), .Q(register_3_q), .clk(clock_4_out));  // open: clr
  Clock clock_4 (.out(clock_4_out));
  registerFiles registerfiles_1 (
    .dwrite(dwrite), .dval(dval), .r0(r0), .r1(r1), .r2(r2), .r3(r3), .sourceregsel(sourceregsel),
    .destregsel(destregsel), .dbus(dbus), .zero(registerfiles_1_zero), .negative(registerfiles_1_negative),
    .sbus(sbus));
  ALU_8bit alu_8bit_1 (
    .A(dbus), .B(sbus), .Select(aluop), .Result(Result), .Zero(Zero), .Negative(Negative),
    .Overflow(Overflow), .Carry(Carry_out));

  // Notes on the sheet:
  //   Dataout Bus
  //   address bus
  //   Immediate
  //   IR
  //   CU
  //   8-bit CPU 
  //   PC Adder
  //   Register 
  //   Files
  //   Source Bus
  //   Register Values
  //   ALU
  //   RESULT
endmodule

module ALU_8bit (
  input  [7:0] A,
  input  [7:0] B,
  input  [1:0] Select,
  output [7:0] Result,
  output Zero,
  output Negative,
  output Overflow,
  output Carry
);

  wire or_1_out;
  wire [7:0] divider_1_q1, main_1_p0, n8_bit_adder_1_s0;

  _8_bit_adder u_8_bit_adder_1 (
    .B0(B[0]), .B1(B[1]), .B2(B[2]), .B3(B[3]), .B4(B[4]), .B5(B[5]), .B6(B[6]), .B7(B[7]), .A0(A[0]),
    .A1(A[1]), .A2(A[2]), .A3(A[3]), .A4(A[4]), .A5(A[5]), .A6(A[6]), .A7(A[7]), .Add_Sub(Select[0]),
    .Co(Carry), .S0(n8_bit_adder_1_s0[0]), .S1(n8_bit_adder_1_s0[1]), .S2(n8_bit_adder_1_s0[2]),
    .S3(n8_bit_adder_1_s0[3]), .S4(n8_bit_adder_1_s0[4]), .S5(n8_bit_adder_1_s0[5]),
    .S6(n8_bit_adder_1_s0[6]), .S7(n8_bit_adder_1_s0[7]), .Overflow(Overflow));  // open: Zero, Negative
  ALU_main main_1 (
    .A7(A[7]), .A6(A[6]), .A5(A[5]), .A4(A[4]), .A3(A[3]), .A2(A[2]), .A1(A[1]), .A0(A[0]), .B7(B[7]),
    .B6(B[6]), .B5(B[5]), .B4(B[4]), .B3(B[3]), .B2(B[2]), .B1(B[1]), .B0(B[0]), .P7(main_1_p0[7]),
    .P6(main_1_p0[6]), .P5(main_1_p0[5]), .P4(main_1_p0[4]), .P3(main_1_p0[3]), .P2(main_1_p0[2]),
    .P1(main_1_p0[1]), .P0(main_1_p0[0]));  // open: out_17, out_18, out_19, out_20, out_21, out_22, out_23, out_24
  Divider divider_1 (
    .A7(A[7]), .A6(A[6]), .A5(A[5]), .A4(A[4]), .A3(A[3]), .A2(A[2]), .A1(A[1]), .A0(A[0]), .B7(B[7]),
    .B6(B[6]), .B5(B[5]), .B4(B[4]), .B3(B[3]), .B2(B[2]), .B1(B[1]), .B0(B[0]), .Q8(divider_1_q1[7]),
    .Q7(divider_1_q1[6]), .Q6(divider_1_q1[5]), .Q5(divider_1_q1[4]), .Q4(divider_1_q1[3]),
    .Q3(divider_1_q1[2]), .Q2(divider_1_q1[1]), .Q1(divider_1_q1[0]));  // open: R7, R6, R5, R4, R3, R2, R1, R0
  Multiplexer #(.select(2), .width(8), .enable("false")) multiplexer_1 (
    .in0(main_1_p0), .in1(divider_1_q1), .in2(n8_bit_adder_1_s0), .in3(n8_bit_adder_1_s0),
    .out({Negative, Result[6:0]}), .sel(Select));
  or or_1 (or_1_out, Result[0], Result[1], Result[2], Result[3], Result[4], Result[5], Result[6], Negative);
  not not_1 (Zero, or_1_out);

  assign Result[7] = Negative;

  // Notes on the sheet:
  //   add/subtract
  //   multiply
  //   divide
  //   ALU
  //   00 - Multiply
  //   01 - Divide
  //   10 - Add
  //   11 - Subtract
endmodule
