// Logisim project CU.circ as structural Verilog: 2 circuits, main circuit Decode Logic
module PC_Adder (
  input  [7:0] PC_in,
  output [7:0] PC_out
);

  Adder adder_1 (.a(PC_in), .b(8'h1), .out(PC_out), .cin(1'b0));  // open: cout

  // Notes on the sheet:
  //   PC Adder
endmodule

module Decode_Logic (
  input  [7:0] irvalue,
  input  zero,
  input  negative,
  output [1:0] destregsel,
  output [1:0] phase,
  output [1:0] sourceregsel,
  output [1:0] aluop,
  output irload,
  output immload,
  output pcsel,
  output pcload,
  output read_write,
  output [1:0] regsel,
  output dwrite,
  output [1:0] addrsel
);

  wire and_1_out, and_2_out, and_3_out, and_4_out, and_5_out, clock_1_out, multiplexer_3_out,
       multiplexer_6_out, not_1_out, not_2_out, not_3_out, not_4_out, or_1_out;
  wire [1:0] multiplexer_1_out, multiplexer_10_out;

  not not_1 (not_1_out, zero);
  not not_2 (not_2_out, negative);
  and and_1 (and_1_out, not_1_out, not_2_out);
  Multiplexer #(.select(4), .width(2), .enable("false")) multiplexer_1 (
    .in0(2'b11), .in1(2'b11), .in2(2'b11), .in3(2'b11), .in4(2'b10), .in5(2'b00), .in6(2'b01), .in7(2'b00),
    .in8(2'b00), .in9(2'b00), .in10(2'b00), .in11(2'b00), .in12(2'b10), .in13(2'b00), .in14(2'b00),
    .in15(2'b00), .out(multiplexer_1_out), .sel(irvalue[7:4]));
  Multiplexer #(.select(2), .enable("false")) multiplexer_2 (
    .in0(1'b1), .in1(1'b0), .in2(1'b0), .in3(1'b0), .out(irload), .sel(phase));
  not not_3 (not_3_out, irvalue[6]);
  Multiplexer #(.select(2), .enable("false")) multiplexer_3 (
    .in0(zero), .in1(not_1_out), .in2(and_1_out), .in3(negative), .out(multiplexer_3_out), .sel(irvalue[5:4]));
  and and_2 (and_2_out, not_3_out, irvalue[7], multiplexer_3_out);
  and and_3 (and_3_out, irvalue[4], irvalue[5], irvalue[6], irvalue[7]);
  Multiplexer #(.select(2), .width(2), .enable("false")) multiplexer_4 (
    .in0(2'b00), .in1(2'b00), .in2(multiplexer_1_out), .in3(2'b00), .out(regsel), .sel(phase));
  or or_1 (or_1_out, and_2_out, and_3_out);
  Multiplexer #(.select(2), .enable("false")) multiplexer_5 (
    .in0(1'b1), .in1(irvalue[7]), .in2(or_1_out), .in3(1'b0), .out(pcload), .sel(phase));
  Multiplexer #(.select(4), .enable("false")) multiplexer_6 (
    .in0(1'b1), .in1(1'b1), .in2(1'b1), .in3(1'b1), .in4(1'b1), .in5(1'b0), .in6(1'b1), .in7(1'b0),
    .in8(1'b0), .in9(1'b0), .in10(1'b0), .in11(1'b0), .in12(1'b1), .in13(1'b0), .in14(1'b1), .in15(1'b0),
    .out(multiplexer_6_out), .sel(irvalue[7:4]));
  Multiplexer #(.select(2), .enable("false")) multiplexer_7 (
    .in0(1'b0), .in1(irvalue[7]), .in2(1'b0), .in3(1'b0), .out(immload), .sel(phase));
  Multiplexer #(.select(2), .enable("false")) multiplexer_8 (
    .in0(1'b0), .in1(1'b0), .in2(multiplexer_6_out), .in3(1'b0), .out(dwrite), .sel(phase));
  Clock clock_1 (.out(clock_1_out));
  not not_4 (not_4_out, irvalue[5]);
  Counter #(.width(2), .max('h3)) counter_1 (
    .Q(phase), .clk(clock_1_out), .clr(and_4_out));  // open: load, D, count, carry
  and and_4 (and_4_out, phase[1], phase[0]);
  Multiplexer #(.select(2), .enable("false")) multiplexer_9 (
    .in0(1'b1), .in1(1'b1), .in2(1'b0), .in3(1'b0), .out(pcsel), .sel(phase));
  and and_5 (and_5_out, irvalue[4], not_4_out, irvalue[6]);
  Multiplexer #(.select(4), .width(2), .enable("false")) multiplexer_10 (
    .in0(2'b00), .in1(2'b00), .in2(2'b00), .in3(2'b00), .in4(2'b10), .in5(2'b10), .in6(2'b00), .in7(2'b00),
    .in8(2'b00), .in9(2'b00), .in10(2'b00), .in11(2'b00), .in12(2'b00), .in13(2'b01), .in14(2'b01),
    .in15(2'b00), .out(multiplexer_10_out), .sel(irvalue[7:4]));
  Multiplexer #(.select(2), .enable("false")) multiplexer_11 (
    .in0(1'b0), .in1(1'b0), .in2(and_5_out), .in3(1'b0), .out(read_write), .sel(phase));
  Multiplexer #(.select(2), .width(2), .enable("false")) multiplexer_12 (
    .in0(2'b00), .in1(2'b00), .in2(multiplexer_10_out), .in3(2'b00), .out(addrsel), .sel(phase));

  assign aluop = irvalue[5:4];
  assign destregsel = irvalue[3:2];
  assign sourceregsel = irvalue[1:0];

  // Other names for the same wires on the sheet: i4 = irvalue[4]; op1op2[3:0] = irvalue[7:4]; op2[1:0] = irvalue[5:4];
  //   i5 = irvalue[5]; i6 = irvalue[6]; op1[1:0] = irvalue[7:6]; i7 = irvalue[7]; rd[1:0] = irvalue[3:2];
  //   rs[1:0] = irvalue[1:0]

  // Notes on the sheet:
  //   IR Load
  //   PC Load
  //   Register Select
  //   Labels 
  //   Control Unit
  //   Immed Load
  //   Dest Reg Write
  //   Phase
  //   Counter
  //   PC Select
  //   Read/Write
  //   Address Select
endmodule
