// Logisim project project.circ as structural Verilog
module pc_adder (
  input  [7:0] PC_input,
  output [7:0] PC_output
);

  Adder adder_1 (.a(PC_input), .b(8'h1), .out(PC_output), .cin(1'b0));  // open: cout
endmodule

module pc_select (
  input  [1:0] Phase,
  output PC_select
);

  Multiplexer #(.select(2), .enable("false")) multiplexer_1 (
    .in0(1'b1), .in1(1'b1), .in2(1'b0), .in3(1'b0), .out(PC_select), .sel(Phase));
endmodule

module pc_load (
  input  [7:0] IRBit,
  input  zero,
  input  [1:0] phase,
  input  negative,
  input  [1:0] op2,
  output PC_Load
);

  wire and_1_out, and_2_out, and_3_out, multiplexer_1_out, not_1_out, not_2_out, not_3_out, or_1_out;

  not not_1 (not_1_out, zero);
  not not_2 (not_2_out, negative);
  and and_1 (and_1_out, not_1_out, not_2_out);
  not not_3 (not_3_out, IRBit[6]);
  Multiplexer #(.select(2), .enable("false")) multiplexer_1 (
    .in0(zero), .in1(not_1_out), .in2(and_1_out), .in3(negative), .out(multiplexer_1_out), .sel(op2));
  and and_2 (and_2_out, IRBit[4], IRBit[5], IRBit[6], IRBit[7]);
  and and_3 (and_3_out, not_3_out, IRBit[7], multiplexer_1_out);
  or or_1 (or_1_out, and_2_out, and_3_out);
  Multiplexer #(.select(2), .enable("false")) multiplexer_2 (
    .in0(1'b1), .in1(IRBit[7]), .in2(or_1_out), .in3(1'b0), .out(PC_Load), .sel(phase));
endmodule
